# Fritzing sketch Ictericia (saved by Fritzing 0.9.3b)
circuit board: 8.28088cm x 5.87963cm
breadboards: 1

parts:
  PD1 = S1133 Si Photodiode [package="8mm Ceramic [THT]"]
  PD2 = S1133 Si Photodiode [package="8mm Ceramic [THT]"]
  PD3 = S1133 Si Photodiode [package="8mm Ceramic [THT]"]
  PD4 = S1133 Si Photodiode [package="8mm Ceramic [THT]"]
  LED2 = LED - 5mm [color="Blue (470nm)" package="5 mm [THT]"]
  LED1 = LED - 5mm [color="Blue (470nm)" package="5 mm [THT]"]
  LED4 = LED - 5mm [color="Green (570nm)" package="5 mm [THT]"]
  LED3 = LED - 5mm [color="Green (570nm)" package="5 mm [THT]"]
  Buzzer = Piezo Speaker
  Switch = Toggle Switch [package=THT]
  R4 = Resistor [tolerance=±5% resistance=100 package="0805 [SMD]"]
  R2 = Resistor [tolerance=±5% resistance=100 package="0805 [SMD]"]
  R3 = Resistor [tolerance=±5% resistance=100 package="0805 [SMD]"]
  R1 = Resistor [tolerance=±5% resistance=100 package="0805 [SMD]"]
  Convertidor_de_Voltaje = Breadboard Power Supply Board SMD
  Batería_9V = Battery block 9V
  Arduino_Nano = Arduino Nano (Rev3.0) (ICSP)
  Display_LCD = Display LCD 2.0 inch 176x220w [form="♀ (female)" package=THT]
  J1 = female pin header, 2 pins [form="♀ (female)"]
  J2 = female pin header, 2 pins [form="♀ (female)"]
  J3 = female pin header, 2 pins [form="♀ (female)"]
  J4 = female pin header, 2 pins [form="♀ (female)"]
  J5 = female pin header, 2 pins [form="♀ (female)"]
  J6 = female pin header, 2 pins [form="♀ (female)"]
  J7 = female pin header, 2 pins [form="♀ (female)"]
  J8 = female pin header, 2 pins [form="♀ (female)"]
  J9 = female pin header, 2 pins [form="♀ (female)"]
  J10 = female pin header, 2 pins [form="♀ (female)"]

nets:
  N1: PD1.cathode, Arduino_Nano.D7, J9.pin2
  GND: PD1.anode, PD2.anode, PD3.anode, PD4.anode, LED2.cathode, LED1.cathode, LED4.cathode, LED3.cathode, Buzzer.pin1, Switch.L1, Convertidor_de_Voltaje.GND, Batería_9V.-, Arduino_Nano.GND, Display_LCD.GND, J1.pin2
  N2: PD2.cathode, Arduino_Nano.D6, J10.pin1
  N3: PD3.cathode, Arduino_Nano.D5, J9.pin1
  N4: PD4.cathode, Arduino_Nano.D4, J10.pin2
  N5: LED2.anode, R2.Pin_0, R2.Pin_1, Arduino_Nano.D10, J5.pin2, J7.pin2
  N6: LED1.anode, R1.Pin_0, R1.Pin_1, Arduino_Nano.D11/MOSI, J5.pin1, J7.pin1
  N7: LED4.anode, R4.Pin_0, R4.Pin_1, Arduino_Nano.D8, J6.pin2, J8.pin2
  N8: LED3.anode, R3.Pin_0, R3.Pin_1, Arduino_Nano.D9, J6.pin1, J8.pin1
  N9: Buzzer.pin2, Arduino_Nano.D12/MISO
  VCC: Switch.COM, Convertidor_de_Voltaje.VCC, Arduino_Nano.5V, Display_LCD.VCC, J1.pin1
  N10: Switch.L2, Arduino_Nano.D3
  N11: Convertidor_de_Voltaje.VIN, Batería_9V.+
  N12: Arduino_Nano.A5, Display_LCD.CS, J4.pin2
  N13: Arduino_Nano.A4, Display_LCD.RST, J4.pin1
  N14: Arduino_Nano.A3, Display_LCD.RS, J3.pin2
  N15: Arduino_Nano.A2, Display_LCD.SDA, J3.pin1
  N16: Arduino_Nano.A1, Display_LCD.CLK, J2.pin2
  N17: Arduino_Nano.A0, Display_LCD.NC, J2.pin1

custom parts:
  Display LCD 2.0 inch 176x220w: Generic female header
